# Fritzing sketch BreadboardCircuit (saved by Fritzing 0.9.3b)
breadboards: 1

parts:
  RELAY = Keyes Relay [package=THT]
  FAN_POWER_SOURCE = Header 2 [package=screwterminal-3.5mm-2_lock]
  ARDUINO_UNO_R3 = Arduino Uno (Rev3)
  RELAY_2 = Keyes Relay [package=THT]
  BULB_2 = LEDs [package=led10mm]
  BULB_1 = LEDs [package=led10mm]
  BULB_POWER_SOURCE = Header 2 [package=screwterminal-3.5mm-2_lock]
  IR_RECEIVER = TSOP312.., 314.. [package=THT]
  LED1 = LED - 3mm [color="Red (633nm)" package="3 mm [THT]"]
  LED2 = LED - 3mm [color="Red (633nm)" package="3 mm [THT]"]
  R1 = Resistor [tolerance=±5% resistance=220 package="0603 [SMD]"]
  R2 = Resistor [tolerance=±5% resistance=220 package="0603 [SMD]"]

nets:
  N1: RELAY.signal, ARDUINO_UNO_R3.D6_PWM
  N2: RELAY.C, BULB_POWER_SOURCE.1
  N3: RELAY.NO, BULB_1.C
  N4: FAN_POWER_SOURCE.1, RELAY_2.C
  N5: FAN_POWER_SOURCE.2, BULB_2.A
  N6: ARDUINO_UNO_R3.D11_PWM/MOSI, R1.Pin_1
  N7: ARDUINO_UNO_R3.D12/MISO, R2.Pin_1
  N8: ARDUINO_UNO_R3.D5_PWM, IR_RECEIVER.Data
  N9: ARDUINO_UNO_R3.D7, RELAY_2.signal
  N10: ARDUINO_UNO_R3.5V, RELAY_2.power, IR_RECEIVER.Vs
  GND: ARDUINO_UNO_R3.GND, RELAY_2.ground, IR_RECEIVER.GND
  N11: RELAY_2.NO, BULB_2.C
  N12: BULB_1.A, BULB_POWER_SOURCE.2
  N13: LED1.cathode, LED2.cathode
  N14: LED1.anode, R2.Pin_0
  N15: LED2.anode, R1.Pin_0

custom parts:
  Keyes Relay: The Keyes 5V relay module is suitable for SCM development, home appliance control. It uses a 5V~12V TIL control signal which can control DC / AC signal.
  LEDs: LEDs Standard schematic elements and footprints for 5mm, 3mm, 1206, and 0603 sized LEDs. 5mm - Spark Fun Electronics SKU : COM-00529 (and others)
